// Logisim project second.circ as structural Verilog: 1 circuit, main circuit main
module main (
  output out_1
);

  wire and_1_out, and_2_out, and_3_out, clock_1_out, not_1_out, or_1_out, or_2_out, or_3_out, or_4_out;
  wire [2:0] counter_1_q, counter_2_q;
  wire [7:0] shift_register_1_q0, shift_register_2_q0;

  Clock clock_1 (.out(clock_1_out));
  Counter #(.width(3), .max('h7)) counter_1 (
    .count(clock_1_out), .Q(counter_1_q), .clk(clock_1_out));  // open: load, D, carry, clr
  Counter #(.width(3), .max('h7)) counter_2 (
    .count(clock_1_out), .Q(counter_2_q), .clk(clock_1_out));  // open: load, D, carry, clr
  or or_1 (or_1_out, ~counter_1_q[1], counter_1_q[2]);  // OR_Gate
  and and_1 (and_1_out, or_1_out, or_2_out);
  or or_2 (or_2_out, counter_1_q[1], ~counter_1_q[2]);  // OR_Gate
  not not_1 (not_1_out, counter_1_q[1]);
  or or_3 (or_3_out, not_1_out, and_1_out);
  or or_4 (or_4_out, ~counter_2_q[1], counter_2_q[2]);  // OR_Gate
  and and_2 (and_2_out, counter_2_q[0], or_4_out);
  and and_3 (and_3_out, counter_1_q[0], or_3_out);
  Shift_Register shift_register_1 (
    .in(and_3_out), .clk(clock_1_out), .q0(shift_register_1_q0[0]), .q1(shift_register_1_q0[1]),
    .q2(shift_register_1_q0[2]), .q3(shift_register_1_q0[3]), .q4(shift_register_1_q0[4]),
    .q5(shift_register_1_q0[5]), .q6(shift_register_1_q0[6]), .q7(shift_register_1_q0[7]));  // open: shift, out, load, clr, d0, d1, d2, d3, d4, d5, d6, d7
  Shift_Register shift_register_2 (
    .in(and_2_out), .clk(clock_1_out), .q0(shift_register_2_q0[0]), .q1(shift_register_2_q0[1]),
    .q2(shift_register_2_q0[2]), .q3(shift_register_2_q0[3]), .q4(shift_register_2_q0[4]),
    .q5(shift_register_2_q0[5]), .q6(shift_register_2_q0[6]), .q7(shift_register_2_q0[7]));  // open: shift, out, load, clr, d0, d1, d2, d3, d4, d5, d6, d7
  Comparator comparator_1 (.a(shift_register_1_q0), .b(shift_register_2_q0), .eq(out_1));  // open: gt, lt
endmodule
