// Logisim project second_prac.circ as structural Verilog: 3 circuits, main circuit main
module main (
  output out_1,
  output out_2,
  output out_3
);

  wire and_1_out, and_2_out, and_3_out, clock_1_out, counter_1_carry, t_ff_1_q, \мднф_1_out_6 ;
  wire [4:0] counter_1_q;
  wire [31:0] shift_register_1_q0;

  Clock clock_1 (.out(clock_1_out));
  Counter #(.width(5), .max('h1f)) counter_1 (
    .Q(counter_1_q), .carry(counter_1_carry), .clk(and_1_out));  // open: load, D, count, clr
  and and_1 (and_1_out, clock_1_out, ~counter_1_carry);  // AND_Gate
  \МДНФ  \u_мднф_1  (
    .x1(counter_1_q[4]), .x2(counter_1_q[3]), .x3(counter_1_q[2]), .x4(counter_1_q[1]), .x5(counter_1_q[0]),
    .out_6(\мднф_1_out_6 ));
  and and_2 (and_2_out, ~t_ff_1_q, counter_1_carry);  // AND_Gate
  T_Flip_Flop t_ff_1 (.clk(clock_1_out), .T(and_2_out), .Q(t_ff_1_q));  // open: Qn, preset, reset, en
  and and_3 (and_3_out, clock_1_out, ~t_ff_1_q);  // AND_Gate
  Shift_Register #(.length(32)) shift_register_1 (
    .in(\мднф_1_out_6 ), .clk(and_3_out), .q0(shift_register_1_q0[0]), .q1(shift_register_1_q0[1]),
    .q2(shift_register_1_q0[2]), .q3(shift_register_1_q0[3]), .q4(shift_register_1_q0[4]),
    .q5(shift_register_1_q0[5]), .q6(shift_register_1_q0[6]), .q7(shift_register_1_q0[7]),
    .q8(shift_register_1_q0[8]), .q9(shift_register_1_q0[9]), .q10(shift_register_1_q0[10]),
    .q11(shift_register_1_q0[11]), .q12(shift_register_1_q0[12]), .q13(shift_register_1_q0[13]),
    .q14(shift_register_1_q0[14]), .q15(shift_register_1_q0[15]), .q16(shift_register_1_q0[16]),
    .q17(shift_register_1_q0[17]), .q18(shift_register_1_q0[18]), .q19(shift_register_1_q0[19]),
    .q20(shift_register_1_q0[20]), .q21(shift_register_1_q0[21]), .q22(shift_register_1_q0[22]),
    .q23(shift_register_1_q0[23]), .q24(shift_register_1_q0[24]), .q25(shift_register_1_q0[25]),
    .q26(shift_register_1_q0[26]), .q27(shift_register_1_q0[27]), .q28(shift_register_1_q0[28]),
    .q29(shift_register_1_q0[29]), .q30(shift_register_1_q0[30]), .q31(shift_register_1_q0[31]));  // open: shift, out, load, clr, d0, d1, d2, d3, d4, d5, d6, d7, d8, d9, d10, d11, d12, d13, d14, d15, d16, d17, d18, d19, d20, d21, d22, d23, d24, d25, d26, d27, d28, d29, d30, d31
  Comparator #(.width(32)) comparator_1 (.a(shift_register_1_q0), .b(32'hf049bd7e), .gt(out_1), .eq(out_2), .lt(out_3));
endmodule

module \МДНФ  (
  input  x1,
  input  x2,
  input  x3,
  input  x4,
  input  x5,
  output out_6
);

  wire and_1_out, and_2_out, and_3_out, and_4_out, and_5_out, and_6_out, and_7_out, and_8_out, and_9_out;

  and and_1 (and_1_out, ~x1, x2, x3, x4, x5);  // AND_Gate
  and and_2 (and_2_out, x2, x3, ~x4, ~x5);  // AND_Gate
  and and_3 (and_3_out, x1, x2, x4, ~x5);  // AND_Gate
  and and_4 (and_4_out, x2, ~x3, ~x4, x5);  // AND_Gate
  and and_5 (and_5_out, ~x1, ~x2, ~x3);  // AND_Gate
  and and_6 (and_6_out, x1, ~x3, x4);  // AND_Gate
  and and_7 (and_7_out, x1, x3, ~x4);  // AND_Gate
  and and_8 (and_8_out, x1, ~x2, x4, x5);  // AND_Gate
  and and_9 (and_9_out, ~x2, ~x3, ~x5);  // AND_Gate
  or or_1 (out_6, and_1_out, and_2_out, and_3_out, and_4_out, and_5_out, and_6_out, and_7_out, and_8_out, and_9_out);
endmodule

module \СКНФ  (
  input  x1,
  input  x2,
  input  x3,
  input  x4,
  input  x5,
  output out_6
);

  wire not_1_out, not_2_out, not_3_out, not_4_out, not_5_out, or_1_out, or_2_out, or_3_out, or_4_out,
       or_5_out, or_6_out, or_7_out, or_8_out, or_9_out, or_10_out, or_11_out, or_12_out, or_13_out;

  not not_1 (not_1_out, x1);
  not not_2 (not_2_out, x2);
  not not_3 (not_3_out, x3);
  not not_4 (not_4_out, x5);
  not not_5 (not_5_out, x4);
  or or_1 (or_1_out, x1, x2, not_3_out, x4, x5);
  or or_2 (or_2_out, x1, x2, not_3_out, x4, not_4_out);
  or or_3 (or_3_out, x1, x2, not_3_out, not_5_out, x5);
  or or_4 (or_4_out, x1, x2, not_3_out, not_5_out, not_4_out);
  or or_5 (or_5_out, x1, not_2_out, x3, x4, x5);
  or or_6 (or_6_out, x1, not_2_out, x3, not_5_out, x5);
  or or_7 (or_7_out, x1, not_2_out, x3, not_5_out, not_4_out);
  or or_8 (or_8_out, x1, not_2_out, not_3_out, x4, not_4_out);
  or or_9 (or_9_out, x1, not_2_out, not_3_out, not_5_out, x5);
  or or_10 (or_10_out, not_1_out, x2, x3, x4, not_4_out);
  or or_11 (or_11_out, not_1_out, x2, not_3_out, not_5_out, x5);
  or or_12 (or_12_out, not_1_out, not_2_out, x3, x4, x5);
  or or_13 (or_13_out, not_1_out, not_2_out, not_3_out, not_5_out, not_4_out);
  and and_1 (out_6, or_1_out, or_2_out, or_3_out, or_4_out, or_5_out, or_6_out, or_7_out, or_8_out, or_9_out, or_10_out, or_11_out, or_12_out, or_13_out);
endmodule
