// Logisim project d-trigger.circ as structural Verilog: 1 circuit, main circuit main
module main (
  output out_1,
  output out_2,
  output out_3,
  output out_4,
  output out_5
);

  wire clock_1_out, nand_1_out, nand_2_out, nand_3_out, nand_4_out, nand_5_out, nand_6_out, nand_7_out,
       nand_8_out, nand_9_out, nand_10_out, nand_11_out, nand_12_out, nand_13_out, nand_14_out, nand_15_out,
       nand_16_out, nand_17_out, nand_18_out, nand_19_out, nand_20_out, not_1_out;

  nand nand_1 (nand_1_out, ~out_2, out_3, ~out_4, ~out_5);  // NAND_Gate
  nand nand_2 (nand_2_out, ~out_2, ~out_3, out_4, out_5);  // NAND_Gate
  nand nand_3 (nand_3_out, ~out_2, ~out_3, ~out_4);  // NAND_Gate
  nand nand_4 (nand_4_out, ~out_2, ~out_3, ~out_5);  // NAND_Gate
  nand nand_5 (nand_5_out, out_2, out_3, out_5);
  nand nand_6 (nand_6_out, out_2, out_3, out_4);
  nand nand_7 (nand_7_out, ~out_1, ~out_2, ~out_3, ~out_5);  // NAND_Gate
  nand nand_8 (nand_8_out, out_2, out_3, ~out_4, ~out_5);  // NAND_Gate
  nand nand_9 (nand_9_out, ~out_3, ~out_4, out_5);  // NAND_Gate
  nand nand_10 (nand_10_out, out_2, ~out_3, out_4);  // NAND_Gate
  nand nand_11 (nand_11_out, ~out_1, ~out_2, ~out_3, ~out_4, out_5);  // NAND_Gate
  nand nand_12 (nand_12_out, ~out_2, ~out_3, out_4, ~out_5);  // NAND_Gate
  nand nand_13 (nand_13_out, out_2, ~out_4, ~out_5);  // NAND_Gate
  nand nand_14 (nand_14_out, out_3, out_4, out_5);
  nand nand_15 (nand_15_out, out_2, out_4, out_5);
  nand nand_16 (nand_16_out, out_1, ~out_5);  // NAND_Gate
  not not_1 (not_1_out, out_5);
  nand nand_17 (nand_17_out, nand_1_out, nand_2_out);
  nand nand_18 (nand_18_out, nand_3_out, nand_4_out, nand_5_out, nand_6_out);
  nand nand_19 (nand_19_out, nand_7_out, nand_8_out, nand_9_out, nand_10_out);
  nand nand_20 (nand_20_out, nand_11_out, nand_12_out, nand_13_out, nand_14_out, nand_15_out, nand_16_out);
  Clock clock_1 (.out(clock_1_out));
  D_Flip_Flop d_ff_1 (.clk(clock_1_out), .D(not_1_out), .Q(out_5));  // open: Qn, preset, en, reset
  D_Flip_Flop d_ff_2 (.clk(clock_1_out), .D(nand_17_out), .Q(out_1));  // open: Qn, preset, en, reset
  D_Flip_Flop d_ff_3 (.clk(clock_1_out), .D(nand_18_out), .Q(out_2));  // open: Qn, preset, en, reset
  D_Flip_Flop d_ff_4 (.clk(clock_1_out), .D(nand_19_out), .Q(out_3));  // open: Qn, preset, en, reset
  D_Flip_Flop d_ff_5 (.clk(clock_1_out), .D(nand_20_out), .Q(out_4));  // open: Qn, preset, en, reset

  // Other names for the same wires on the sheet: Q0 = out_5; Q1 = out_4; Q2 = out_3; Q3 = out_2; Q4 = out_1
endmodule
