// Logisim project jk-trigger+def.circ as structural Verilog: 1 circuit, main circuit main
module main (
  input  in_1,
  input  in_2,
  input  in_3,
  output out_4,
  output out_5,
  output out_6,
  output out_7,
  output out_8,
  output out_9,
  output out_10,
  output out_11
);

  wire clock_1_out, decoder_1_out0, decoder_1_out1, decoder_1_out2, decoder_1_out3, decoder_1_out4,
       decoder_1_out5, decoder_1_out6, decoder_1_out7, nor_1_out, nor_2_out, nor_3_out, nor_4_out, nor_5_out,
       nor_6_out, nor_7_out, nor_8_out, nor_9_out, nor_10_out, nor_11_out, nor_12_out, nor_13_out,
       nor_14_out, nor_15_out, nor_16_out, nor_17_out, nor_18_out, nor_19_out, nor_20_out, nor_21_out,
       nor_22_out, nor_23_out, nor_24_out;

  nor nor_1 (nor_1_out, out_9, out_11);
  nor nor_2 (nor_2_out, out_10, ~out_11);  // NOR_Gate
  nor nor_3 (nor_3_out, ~out_9, ~out_10);  // NOR_Gate
  nor nor_4 (nor_4_out, ~out_10, ~out_11);  // NOR_Gate
  nor nor_5 (nor_5_out, ~out_9, ~out_11);  // NOR_Gate
  nor nor_6 (nor_6_out, ~out_9, ~out_10);  // NOR_Gate
  nor nor_7 (nor_7_out, ~out_8, out_10, out_11);  // NOR_Gate
  nor nor_8 (nor_8_out, out_8, ~out_10, ~out_11);  // NOR_Gate
  nor nor_9 (nor_9_out, ~out_7, out_11);  // NOR_Gate
  nor nor_10 (nor_10_out, ~out_8, out_10, out_11);  // NOR_Gate
  nor nor_11 (nor_11_out, out_7, out_8, out_11);
  nor nor_12 (nor_12_out, ~out_9, ~out_11);  // NOR_Gate
  nor nor_13 (nor_13_out, ~out_8, ~out_11);  // NOR_Gate
  nor nor_14 (nor_14_out, ~out_7, ~out_11);  // NOR_Gate
  nor nor_15 (nor_15_out, out_8, out_9, out_11);
  nor nor_16 (nor_16_out, ~out_9, ~out_11);  // NOR_Gate
  nor nor_17 (nor_17_out, ~out_8, ~out_11);  // NOR_Gate
  Clock clock_1 (.out(clock_1_out));
  nor nor_18 (nor_18_out, nor_1_out, nor_2_out, nor_3_out, out_8);
  nor nor_19 (nor_19_out, nor_4_out, out_9);
  nor nor_20 (nor_20_out, nor_5_out, nor_6_out);
  nor nor_21 (nor_21_out, nor_7_out, nor_8_out, nor_9_out);
  nor nor_22 (nor_22_out, nor_10_out, nor_10_out, nor_10_out);
  nor nor_23 (nor_23_out, nor_11_out, nor_12_out, nor_13_out, nor_14_out);
  nor nor_24 (nor_24_out, nor_15_out, nor_16_out, nor_17_out);
  J_K_Flip_Flop S4 (.J(nor_18_out), .clk(clock_1_out), .K(1'b1), .Q(out_7));  // open: Qn, preset, en, reset
  J_K_Flip_Flop S3 (.J(nor_19_out), .clk(clock_1_out), .K(nor_20_out), .Q(out_8));  // open: Qn, preset, en, reset
  J_K_Flip_Flop S2 (.J(nor_21_out), .clk(clock_1_out), .K(nor_22_out), .Q(out_9));  // open: Qn, preset, en, reset
  J_K_Flip_Flop S1 (.J(nor_23_out), .clk(clock_1_out), .K(nor_24_out), .Q(out_10));  // open: Qn, preset, en, reset
  J_K_Flip_Flop S0 (.J(1'b1), .clk(clock_1_out), .K(1'b1), .Q(out_11));  // open: Qn, preset, en, reset
  Decoder #(.select(3), .enable("false")) decoder_1 (
    .out0(decoder_1_out0), .out1(decoder_1_out1), .out2(decoder_1_out2), .out3(decoder_1_out3),
    .out4(decoder_1_out4), .out5(decoder_1_out5), .out6(decoder_1_out6), .out7(decoder_1_out7),
    .sel({out_6, out_5, out_4}));
  Priority_Encoder priority_encoder_1 (
    .in0(decoder_1_out3), .in1(decoder_1_out1), .in2(decoder_1_out0), .in3(decoder_1_out5),
    .in4(decoder_1_out6), .in5(decoder_1_out7), .in6(decoder_1_out2), .in7(decoder_1_out4),
    .out({in_3, in_2, in_1}));  // open: en_in, gs, en_out

  // Other names for the same wires on the sheet: Q0 = out_11; Q1 = out_10; Q2 = out_9; Q3 = out_8; Q4 = out_7
endmodule
