// Logisim project Задание 1_2.circ as structural Verilog: 1 circuit, main circuit main
module main (
  input  in_1,
  output out_2
);

  wire clock_1_out;
  wire [2:0] register_1_q, rom_1_data;

  ROM #(.addrWidth(4), .dataWidth(3)) rom_1 (.addr({register_1_q, in_1}), .data(rom_1_data));  // open: sel
  Clock clock_1 (.out(clock_1_out));
  Register #(.width(3)) register_1 (.D(rom_1_data), .Q(register_1_q), .clk(clock_1_out));  // open: en, clr
  ROM #(.addrWidth(3), .dataWidth(1)) rom_2 (.addr(register_1_q), .data(out_2));  // open: sel

  // Notes on the sheet:
  //   contents of rom_1 (hex, n*v repeats v):
  //   1 3 2 3 2 3 1 4 1 4
  //   contents of rom_2 (hex, n*v repeats v):
  //   0 0 1 0 1
endmodule
