// Logisim project Задание 2_11.circ as structural Verilog: 2 circuits, main circuit main
module main (
  input  in_1,
  input  in_2,
  output out_3
);

  wire clock_1_out, local_fsm_1_out, undriven;

  Clock clock_1 (.out(clock_1_out));
  local_fsm local_fsm_1 (.IN1(in_1), .IN2(in_2), .CLK(clock_1_out), .OUT(local_fsm_1_out));
  or or_1 (out_3, local_fsm_1_out, undriven);

  // Notes on the sheet:
  //   стробу любой длительности
  //   Индикация события: после нулей на обеих линиях
  //   по каждой из линий IN1 и IN2 прошло ровно по одному
endmodule

module local_fsm (
  input  IN1,
  input  IN2,
  input  CLK,
  output OUT
);

  wire rom_2_data;
  wire [2:0] rom_1_data;
  wire [4:2] register_1_q;

  ROM #(.addrWidth(5), .dataWidth(3)) rom_1 (.addr({register_1_q, IN1, IN2}), .data(rom_1_data));  // open: sel
  Register #(.width(3)) register_1 (.D(rom_1_data), .Q(register_1_q), .clk(CLK));  // open: en, clr
  ROM #(.addrWidth(5), .dataWidth(1)) rom_2 (.addr({register_1_q, IN1, IN2}), .data(rom_2_data));  // open: sel
  D_Flip_Flop d_ff_1 (.clk(CLK), .D(rom_2_data), .Q(OUT));  // open: Qn, preset, en, reset

  // Notes on the sheet:
  //   contents of rom_1 (hex, n*v repeats v):
  //   1 0 0 0 1 0 2 0 3 4 2 5 3 4 2 0 1 4 0 0 1 4 6 5 1 0 6
  //   contents of rom_2 (hex, n*v repeats v):
  //   16*0 1 0 0 0 1 0 0 0 1
endmodule
