// Logisim project Задание 3_1.circ as structural Verilog: 3 circuits, main circuit main
module main (
  input  in_1,
  input  in_2,
  output out_3
);

  wire autother_1_out_4, autother_2_out_4, clock_1_out;

  Clock clock_1 (.out(clock_1_out));
  autother autother_1 (.in_1(clock_1_out), .in_2(out_3), .in_3(in_1), .out_4(autother_1_out_4));
  autother autother_2 (.in_1(clock_1_out), .in_2(out_3), .in_3(in_2), .out_4(autother_2_out_4));
  and and_1 (out_3, autother_1_out_4, autother_2_out_4);
endmodule

module aut (
  input  in_1,
  input  [1:0] in_2,
  output out_3
);

  wire and_1_out, and_2_out, or_1_out, or_2_out, rom_1_data, rom_2_data;
  wire [2:2] d_ff_1_q, d_ff_2_q;

  ROM #(.addrWidth(3), .dataWidth(1)) rom_1 (.addr({d_ff_1_q[2], in_2}), .data(rom_1_data));  // open: sel
  ROM #(.addrWidth(3), .dataWidth(1)) rom_2 (.addr({d_ff_2_q[2], in_2}), .data(rom_2_data));  // open: sel
  and and_1 (and_1_out, rom_1_data, ~d_ff_2_q[2]);  // AND_Gate
  and and_2 (and_2_out, rom_2_data, ~d_ff_1_q[2]);  // AND_Gate
  D_Flip_Flop d_ff_1 (.clk(in_1), .D(and_1_out), .Q(d_ff_1_q[2]));  // open: Qn, preset, en, reset
  D_Flip_Flop d_ff_2 (.clk(in_1), .D(and_2_out), .Q(d_ff_2_q[2]));  // open: Qn, preset, en, reset
  or or_1 (or_1_out, d_ff_1_q[2], in_2[0]);
  or or_2 (or_2_out, in_2[1], d_ff_2_q[2]);
  and and_3 (out_3, or_1_out, or_2_out);

  // Notes on the sheet:
  //   contents of rom_1 (hex, n*v repeats v):
  //   0 1 0 0 4*1
  //   contents of rom_2 (hex, n*v repeats v):
  //   0 0 1 0 4*1
endmodule

module autother (
  input  in_1,
  input  in_2,
  input  in_3,
  output out_4
);

  wire and_1_out, d_ff_1_q, or_1_out;

  and and_1 (and_1_out, ~in_2, in_3);  // AND_Gate
  or or_1 (or_1_out, and_1_out, d_ff_1_q);
  D_Flip_Flop d_ff_1 (.clk(in_1), .D(or_1_out), .Q(d_ff_1_q));  // open: Qn, preset, en, reset
  or or_2 (out_4, in_3, d_ff_1_q);
endmodule
