// Logisim project Задание 4_2.circ as structural Verilog: 1 circuit, main circuit main
module main (
  input  in_1
);

  wire clock_1_out;
  wire [1:0] counter_1_q;
  wire [2:0] register_1_q, rom_1_data;

  Clock clock_1 (.out(clock_1_out));
  Counter #(.width(2), .max('h2)) counter_1 (.Q(counter_1_q), .clk(clock_1_out));  // open: load, D, count, carry, clr
  ROM #(.addrWidth(6), .dataWidth(3)) rom_1 (.addr({register_1_q, in_1, counter_1_q}), .data(rom_1_data));  // open: sel
  Register #(.width(3)) register_1 (.D(rom_1_data), .Q(register_1_q), .clk(clock_1_out));  // open: en, clr
  Hex_Digit_Display hex_digit_display_1 (.value({1'b0, register_1_q}));  // open: dp

  // Notes on the sheet:
  //   contents of rom_1 (hex, n*v repeats v):
  //   4*0 1 2 4 0 4*1 2 3 5 1 4*2 3 4 6 2 4*3 4 5 0 3 4*4 5 6 1 4 4*5 6 0 2 5 4*6 0 1 3 6
endmodule
